# Fritzing sketch SousVideShield (saved by Fritzing 0.7.1b)
stripboards: 1

parts:
  R1 = Resistor [tolerance=±5% resistance=10k package=THT]
  R2 = Resistor [tolerance=±5% resistance=10k package=THT]
  R3 = Resistor [tolerance=±5% resistance=2k package=THT]
  J2 = Screw terminal - 2 pins [package=THT]
  IC1 = IC, DIP package, 8 pins [chip_label=NTE928m spacing=300mil]
  R4 = Resistor [tolerance=±5% resistance=100k package=THT]
  R5 = Resistor [tolerance=±5% resistance=100k package=THT]
  R6 = Resistor [tolerance=±5% resistance=2k package=THT]
  Arduino1 = Arduino

nets:
  N1: R1.Pin_0, R2.Pin_0, IC1.pin8, Arduino1.+5V
  N2: R1.Pin_1, R3.Pin_0, R6.Pin_0
  N3: R2.Pin_1, J2.pin1, IC1.pin3, R5.Pin_0
  N4: R3.Pin_1, J2.pin2, IC1.pin4, R5.Pin_1, R6.Pin_1, Arduino1.GND
  N5: IC1.pin1, R4.Pin_0, Arduino1.A5
  N6: IC1.pin2, R4.Pin_1
